# Fritzing sketch dht11-test-scheme (saved by Fritzing 0.9.3b)
breadboards: 1

parts:
  Part1 = Arduino Uno (Rev3)
  R1 = Resistor [tolerance=±5% resistance=4.7k package=THT]
  RHT1 = Humidity and Temperature Sensor RHT03

nets:
  N1: Part1.D4, R1.Pin_0, RHT1.Data-signal
  5V: Part1.5V, R1.Pin_1, RHT1.Vcc
  N2: Part1.GND, RHT1.GND_2
