# Fritzing sketch hc-sr501-test (saved by Fritzing 0.9.3b)
breadboards: 1

parts:
  Part1 = Arduino Uno (Rev3)
  LED1 = LED - 5mm [color="Red (633nm)" package="5 mm [THT]"]
  R1 = Resistor [tolerance=±5% resistance=220 package=THT]
  Part2 = HC-SR501 Body Sensor Module

nets:
  N1: Part1.D9_PWM, LED1.anode
  N2: Part1.D5_PWM, Part2.OUT
  5V: Part1.5V, Part2.VCC
  GND: Part1.GND, R1.Pin_0, Part2.GND
  N3: LED1.cathode, R1.Pin_1

custom parts:
  HC-SR501 Body Sensor Module: Pyroelectric Infrared PIR Motion Sensor Detector Module
