# Fritzing sketch ky-037-scheme (saved by Fritzing 1.0.1rc)
breadboards: 1

parts:
  Part1 = Arduino Uno (Rev3)
  Part2 = KY-037 High Sensitivity Sound Detection Module [package="Breakout board"]

nets:
  N1: Part1.A0, Part2.A0
  N2: Part1.D3_PWM, Part2.D0
  N3: Part1.5V, Part2.+
  N4: Part1.GND, Part2.G

custom parts:
  KY-037 High Sensitivity Sound Detection Module: KY-037 high sensitivity sound detection module is an analog/digital sensor that uses a condenser microphone to observe changes in environment noise.
